# Fritzing sketch arduino_sketch (saved by Fritzing 0.9.3b)
breadboards: 1

parts:
  Part1 = Arduino Uno (Rev3)
  VCC1 = 4 x AAA Battery Mount
  Part2 = ws2812b [package="smd 2812b"]
  C1 = Electrolytic Capacitor [capacitance=1µF package="100 mil [THT, electrolytic]"]
  R1 = Resistor [tolerance=±5% resistance=470 package="1206 [SMD]"]

nets:
  N1: Part1.D6_PWM, R1.Pin_0
  GND: Part1.GND, VCC1.-, Part2.VSS, C1.-
  N2: VCC1.+, Part2.VDD, C1.+
  N3: Part2.DIN, R1.Pin_1

notes:
  Connect to router via USB
